// Logisim project Atividade.circ as structural Verilog: 1 circuit, main circuit main
module main (
  input  A,
  input  B,
  input  C,
  input  D,
  input  A_2,
  input  B_2,
  input  C_2,
  input  A_3,
  input  B_3,
  input  C_3,
  input  D_2,
  output out_12,
  output out_13,
  output out_14
);

  wire and_2_out, and_3_out, and_4_out, nand_1_out, nand_2_out, nor_1_out, nor_2_out, nor_3_out, nor_4_out,
       not_1_out, not_2_out, or_1_out, or_2_out, or_3_out, xnor_1_out;

  nor nor_1 (nor_1_out, A, ~B, C);  // NOR_Gate
  or or_1 (or_1_out, A, ~D, B);  // OR_Gate
  or or_2 (or_2_out, ~A_3, B_3);  // OR_Gate
  or or_3 (or_3_out, C_3, ~D_2);  // OR_Gate
  nand nand_1 (nand_1_out, ~B_3, D_2);  // NAND_Gate
  nor nor_2 (nor_2_out, nand_1_out, D_2);
  nand nand_2 (nand_2_out, nor_1_out, or_1_out);
  and and_1 (out_13, nand_2_out, and_2_out);
  and and_2 (and_2_out, ~A, B, ~C);  // AND_Gate
  xnor xnor_1 (xnor_1_out, or_2_out, or_3_out);
  not not_1 (not_1_out, xnor_1_out);
  not not_2 (not_2_out, D_2);
  or or_4 (out_14, not_1_out, not_2_out, nor_2_out);
  nor nor_3 (nor_3_out, A_2, C_2);
  and and_3 (and_3_out, nor_3_out, ~B_2);  // AND_Gate
  and and_4 (and_4_out, ~A_2, ~B_2, C_2);  // AND_Gate
  nor nor_4 (nor_4_out, and_3_out, and_4_out);
  and and_5 (out_12, nor_4_out, ~A_2);  // AND_Gate
endmodule
