// Logisim project Atividade1.circ as structural Verilog: 1 circuit, main circuit main
module main (
  input  A,
  input  B,
  input  C,
  input  A_2,
  input  B_2,
  input  C_2,
  output out_7,
  output out_8
);

  wire and_1_out, and_2_out, and_3_out, and_4_out, and_5_out, and_6_out;

  and and_1 (and_1_out, ~A, ~B, ~C);  // AND_Gate
  and and_2 (and_2_out, ~A, ~B, C);  // AND_Gate
  and and_3 (and_3_out, ~A, B, C);  // AND_Gate
  and and_4 (and_4_out, A, ~B, C);  // AND_Gate
  and and_5 (and_5_out, A, B, C);
  and and_6 (and_6_out, ~A_2, ~B_2);  // AND_Gate
  or or_1 (out_8, and_6_out, C_2);
  or or_2 (out_7, and_1_out, and_2_out, and_3_out, and_4_out, and_5_out);
endmodule
