// Logisim project Projeto.circ as structural Verilog: 1 circuit, main circuit main
module main (
  input  A,
  input  B,
  input  C,
  input  D,
  input  A_2,
  input  B_2,
  input  C_2,
  input  A_3,
  input  B_3,
  input  C_3,
  input  D_2,
  input  A_4,
  input  B_4,
  input  C_4,
  input  D_3,
  input  E,
  output out_17,
  output out_18,
  output out_19,
  output out_20
);

  wire and_3_out, and_4_out, and_5_out, and_6_out, and_7_out, and_8_out, nand_1_out, nand_2_out, nand_3_out,
       nor_1_out, nor_2_out, or_1_out, or_2_out, or_3_out, or_4_out, or_6_out;

  or or_1 (or_1_out, A, B);
  or or_2 (or_2_out, B, D);
  nor nor_1 (nor_1_out, ~A_3, B_3);  // NOR_Gate
  nand nand_1 (nand_1_out, ~C_3, D_2);  // NAND_Gate
  and and_1 (out_18, or_1_out, C, or_2_out);
  or or_3 (or_3_out, nor_1_out, nand_1_out);
  and and_2 (out_19, or_3_out, ~D_2);  // AND_Gate
  and and_3 (and_3_out, A_2, B_2, C_2);
  or or_4 (or_4_out, B_2, A_2);
  and and_4 (and_4_out, C_2, or_4_out);
  nand nand_2 (nand_2_out, ~A_4, B_4);  // NAND_Gate
  nand nand_3 (nand_3_out, C_4, ~D_3);  // NAND_Gate
  and and_5 (and_5_out, A_4, ~D_3, ~E);  // AND_Gate
  and and_6 (and_6_out, C_4, D_3, E);
  or or_5 (out_17, and_3_out, and_4_out);
  nor nor_2 (nor_2_out, nand_2_out, nand_3_out);
  or or_6 (or_6_out, and_5_out, and_6_out);
  and and_7 (and_7_out, nor_2_out, E);
  and and_8 (and_8_out, ~A_4, or_6_out);  // AND_Gate
  or or_7 (out_20, and_7_out, and_8_out);
endmodule
