// Logisim project CarryLookAhead.circ as structural Verilog: 1 circuit, main circuit main
module main (
  input  [7:0] A,
  input  [7:0] B,
  input  Op,
  output OverFlow,
  output [7:0] S
);

  wire and_1_out, and_2_out, and_3_out, and_4_out, and_5_out, and_6_out, and_7_out, and_8_out, and_9_out,
       and_10_out, and_11_out, and_12_out, and_13_out, and_14_out, and_15_out, and_16_out, and_17_out,
       and_18_out, and_19_out, and_20_out, and_21_out, and_22_out, and_23_out, and_24_out, and_25_out,
       and_26_out, and_27_out, and_28_out, and_29_out, and_30_out, and_31_out, and_32_out, and_33_out,
       and_34_out, and_35_out, and_36_out, C1_out, C2_out, C3_out, C4_out, C5_out, C6_out, C7_out;
  wire [7:0] G_out, P_out, xor_1_out;

  // Probe on A
  // Probe on B
  assign xor_1_out = B ^ {8{Op}};  // XOR_Gate xor_1, 8 bits wide
  // Probe on S
  // Probe on S
  assign G_out = xor_1_out & A;  // AND_Gate G, 8 bits wide
  assign P_out = xor_1_out | A;  // OR_Gate P, 8 bits wide
  ContadorLookAhead_main main_1 (.S(S[0]), .A(A[0]), .B(xor_1_out[0]), .Cin(Op));
  and and_1 (and_1_out, Op, P_out[0]);
  or C1 (C1_out, and_1_out, G_out[0]);
  ContadorLookAhead_main main_2 (.S(S[1]), .A(A[1]), .B(xor_1_out[1]), .Cin(C1_out));
  and and_2 (and_2_out, Op, P_out[0], P_out[1]);
  and and_3 (and_3_out, G_out[0], P_out[1]);
  or C2 (C2_out, and_2_out, and_3_out, G_out[1]);
  ContadorLookAhead_main main_3 (.S(S[2]), .A(A[2]), .B(xor_1_out[2]), .Cin(C2_out));
  and and_4 (and_4_out, Op, P_out[0], P_out[1], P_out[2]);
  and and_5 (and_5_out, G_out[0], P_out[1], P_out[2]);
  and and_6 (and_6_out, G_out[1], P_out[2]);
  or C3 (C3_out, and_4_out, and_5_out, and_6_out, G_out[2]);
  ContadorLookAhead_main main_4 (.S(S[3]), .A(A[3]), .B(xor_1_out[3]), .Cin(C3_out));
  and and_7 (and_7_out, Op, P_out[0], P_out[1], P_out[2], P_out[3]);
  and and_8 (and_8_out, G_out[0], P_out[1], P_out[2], P_out[3]);
  and and_9 (and_9_out, G_out[1], P_out[2], P_out[3]);
  and and_10 (and_10_out, G_out[2], P_out[3]);
  or C4 (C4_out, and_7_out, and_8_out, and_9_out, and_10_out, G_out[3]);
  and and_11 (and_11_out, Op, P_out[0], P_out[1], P_out[2], P_out[3], P_out[4]);
  ContadorLookAhead_main main_5 (.S(S[4]), .A(A[4]), .B(xor_1_out[4]), .Cin(C4_out));
  and and_12 (and_12_out, G_out[0], P_out[1], P_out[2], P_out[3], P_out[4]);
  and and_13 (and_13_out, G_out[1], P_out[2], P_out[3], P_out[4]);
  and and_14 (and_14_out, G_out[2], P_out[3], P_out[4]);
  and and_15 (and_15_out, G_out[3], P_out[4]);
  or C5 (C5_out, and_11_out, and_12_out, and_13_out, and_14_out, and_15_out, G_out[4]);
  ContadorLookAhead_main main_6 (.S(S[5]), .A(A[5]), .B(xor_1_out[5]), .Cin(C5_out));
  and and_16 (and_16_out, Op, P_out[0], P_out[1], P_out[2], P_out[3], P_out[4], P_out[5]);
  and and_17 (and_17_out, G_out[0], P_out[1], P_out[2], P_out[3], P_out[4], P_out[5]);
  and and_18 (and_18_out, G_out[1], P_out[2], P_out[3], P_out[4], P_out[5]);
  and and_19 (and_19_out, G_out[3], P_out[4], P_out[5]);
  and and_20 (and_20_out, G_out[2], P_out[3], P_out[4], P_out[5]);
  and and_21 (and_21_out, G_out[4], P_out[5]);
  or C6 (C6_out, and_16_out, and_17_out, and_18_out, and_20_out, and_19_out, and_21_out, G_out[5]);
  and and_22 (and_22_out, Op, P_out[0], P_out[1], P_out[2], P_out[3], P_out[4], P_out[5], P_out[6]);
  ContadorLookAhead_main main_7 (.S(S[6]), .A(A[6]), .B(xor_1_out[6]), .Cin(C6_out));
  and and_23 (and_23_out, G_out[0], P_out[1], P_out[2], P_out[3], P_out[4], P_out[5], P_out[6]);
  and and_24 (and_24_out, G_out[2], P_out[3], P_out[4], P_out[5], P_out[6]);
  and and_25 (and_25_out, G_out[1], P_out[2], P_out[3], P_out[4], P_out[5], P_out[6]);
  and and_26 (and_26_out, G_out[3], P_out[4], P_out[5], P_out[6]);
  and and_27 (and_27_out, G_out[5], P_out[6]);
  and and_28 (and_28_out, G_out[4], P_out[5], P_out[6]);
  or C7 (C7_out, and_22_out, and_23_out, and_25_out, and_24_out, and_26_out, and_28_out, and_27_out, G_out[6]);
  ContadorLookAhead_main main_8 (.S(S[7]), .A(A[7]), .B(xor_1_out[7]), .Cin(C7_out));
  and and_29 (and_29_out, Op, P_out[0], P_out[1], P_out[2], P_out[3], P_out[4], P_out[5], P_out[6], P_out[7]);
  and and_30 (and_30_out, G_out[0], P_out[1], P_out[2], P_out[3], P_out[4], P_out[5], P_out[6], P_out[7]);
  and and_31 (and_31_out, G_out[1], P_out[2], P_out[3], P_out[4], P_out[5], P_out[6], P_out[7]);
  and and_32 (and_32_out, G_out[2], P_out[3], P_out[4], P_out[5], P_out[6], P_out[7]);
  and and_33 (and_33_out, G_out[3], P_out[4], P_out[5], P_out[6], P_out[7]);
  and and_34 (and_34_out, G_out[4], P_out[5], P_out[6], P_out[7]);
  and and_35 (and_35_out, G_out[6], P_out[7]);
  and and_36 (and_36_out, G_out[5], P_out[6], P_out[7]);
  or C8 (OverFlow, and_29_out, and_30_out, and_31_out, and_32_out, and_33_out, and_34_out, and_36_out, and_35_out, G_out[7]);
endmodule
