// Logisim project Temporizador.circ as structural Verilog
module Tempo (
);

  wire and_1_out, clock_1_out, j_k_ff_1_q, j_k_ff_2_q, j_k_ff_3_q, j_k_ff_4_q;
  wire [3:0] j_k_ff_1_qn;

  Clock clock_1 (.out(clock_1_out));
  Hex_Digit_Display hex_digit_display_1 (.value(j_k_ff_1_qn));  // open: dp
  and and_1 (and_1_out, j_k_ff_1_q, j_k_ff_2_q, ~j_k_ff_3_q, j_k_ff_4_q);  // AND_Gate
  J_K_Flip_Flop j_k_ff_1 (
    .J(1'b1), .clk(clock_1_out), .K(1'b1), .Q(j_k_ff_1_q), .Qn(j_k_ff_1_qn[0]), .reset(and_1_out));  // open: preset, en
  J_K_Flip_Flop j_k_ff_2 (
    .J(1'b1), .clk(j_k_ff_1_q), .K(1'b1), .Q(j_k_ff_2_q), .Qn(j_k_ff_1_qn[1]), .preset(and_1_out));  // open: en, reset
  J_K_Flip_Flop j_k_ff_3 (
    .J(1'b1), .clk(j_k_ff_2_q), .K(1'b1), .Q(j_k_ff_3_q), .Qn(j_k_ff_1_qn[2]), .reset(and_1_out));  // open: preset, en
  J_K_Flip_Flop j_k_ff_4 (
    .J(1'b1), .clk(j_k_ff_3_q), .K(1'b1), .Q(j_k_ff_4_q), .Qn(j_k_ff_1_qn[3]), .reset(and_1_out));  // open: preset, en
endmodule
