// Logisim project Relogio.circ as structural Verilog: 3 circuits, main circuit main
module main (
);

  wire and_1_out, and_2_out, and_3_out, clock_1_out, n7_segmentos_1_a, n7_segmentos_1_b, n7_segmentos_1_c,
       n7_segmentos_1_d, n7_segmentos_1_e, n7_segmentos_1_f, n7_segmentos_1_g, n7_segmentos_2_a,
       n7_segmentos_2_b, n7_segmentos_2_c, n7_segmentos_2_d, n7_segmentos_2_e, n7_segmentos_2_f,
       n7_segmentos_2_g, n7_segmentos_3_a, n7_segmentos_3_b, n7_segmentos_3_c, n7_segmentos_3_d,
       n7_segmentos_3_e, n7_segmentos_3_f, n7_segmentos_3_g, n7_segmentos_4_a, n7_segmentos_4_b,
       n7_segmentos_4_c, n7_segmentos_4_d, n7_segmentos_4_e, n7_segmentos_4_f, n7_segmentos_4_g,
       n7_segmentos_5_a, n7_segmentos_5_b, n7_segmentos_5_c, n7_segmentos_5_d, n7_segmentos_5_e,
       n7_segmentos_5_f, n7_segmentos_5_g, n7_segmentos_6_a, n7_segmentos_6_b, n7_segmentos_6_c,
       n7_segmentos_6_d, n7_segmentos_6_e, n7_segmentos_6_f, n7_segmentos_6_g;
  wire [3:0] decoder60_1_dezena, decoder60_1_unidade, decoder60_2_dezena, decoder60_2_unidade,
       decoder60_3_dezena, decoder60_3_unidade;
  wire [5:0] j_k_ff_1_q, j_k_ff_2_q, j_k_ff_3_q;

  _7_Segment_Display u_7_segment_display_1 (
    .g(n7_segmentos_1_g), .f(n7_segmentos_1_f), .a(n7_segmentos_1_a), .b(n7_segmentos_1_b),
    .e(n7_segmentos_1_e), .d(n7_segmentos_1_d), .c(n7_segmentos_1_c));  // open: dp
  _7_segmentos u_7_segmentos_1 (
    .in_1(decoder60_3_dezena), .a(n7_segmentos_1_a), .b(n7_segmentos_1_b), .c(n7_segmentos_1_c),
    .d(n7_segmentos_1_d), .e(n7_segmentos_1_e), .f(n7_segmentos_1_f), .g(n7_segmentos_1_g));
  _7_Segment_Display u_7_segment_display_2 (
    .g(n7_segmentos_2_g), .f(n7_segmentos_2_f), .a(n7_segmentos_2_a), .b(n7_segmentos_2_b),
    .e(n7_segmentos_2_e), .d(n7_segmentos_2_d), .c(n7_segmentos_2_c), .dp(1'b1));
  _7_segmentos u_7_segmentos_2 (
    .in_1(decoder60_3_unidade), .a(n7_segmentos_2_a), .b(n7_segmentos_2_b), .c(n7_segmentos_2_c),
    .d(n7_segmentos_2_d), .e(n7_segmentos_2_e), .f(n7_segmentos_2_f), .g(n7_segmentos_2_g));
  _7_Segment_Display u_7_segment_display_3 (
    .g(n7_segmentos_3_g), .f(n7_segmentos_3_f), .a(n7_segmentos_3_a), .b(n7_segmentos_3_b),
    .e(n7_segmentos_3_e), .d(n7_segmentos_3_d), .c(n7_segmentos_3_c));  // open: dp
  _7_segmentos u_7_segmentos_3 (
    .in_1(decoder60_2_dezena), .a(n7_segmentos_3_a), .b(n7_segmentos_3_b), .c(n7_segmentos_3_c),
    .d(n7_segmentos_3_d), .e(n7_segmentos_3_e), .f(n7_segmentos_3_f), .g(n7_segmentos_3_g));
  _7_Segment_Display u_7_segment_display_4 (
    .g(n7_segmentos_5_g), .f(n7_segmentos_5_f), .a(n7_segmentos_5_a), .b(n7_segmentos_5_b),
    .e(n7_segmentos_5_e), .d(n7_segmentos_5_d), .c(n7_segmentos_5_c));  // open: dp
  _7_Segment_Display u_7_segment_display_5 (
    .g(n7_segmentos_4_g), .f(n7_segmentos_4_f), .a(n7_segmentos_4_a), .b(n7_segmentos_4_b),
    .e(n7_segmentos_4_e), .d(n7_segmentos_4_d), .c(n7_segmentos_4_c), .dp(1'b1));
  _7_segmentos u_7_segmentos_4 (
    .in_1(decoder60_2_unidade), .a(n7_segmentos_4_a), .b(n7_segmentos_4_b), .c(n7_segmentos_4_c),
    .d(n7_segmentos_4_d), .e(n7_segmentos_4_e), .f(n7_segmentos_4_f), .g(n7_segmentos_4_g));
  _7_Segment_Display u_7_segment_display_6 (
    .g(n7_segmentos_6_g), .f(n7_segmentos_6_f), .a(n7_segmentos_6_a), .b(n7_segmentos_6_b),
    .e(n7_segmentos_6_e), .d(n7_segmentos_6_d), .c(n7_segmentos_6_c));  // open: dp
  _7_segmentos u_7_segmentos_5 (
    .in_1(decoder60_1_dezena), .a(n7_segmentos_5_a), .b(n7_segmentos_5_b), .c(n7_segmentos_5_c),
    .d(n7_segmentos_5_d), .e(n7_segmentos_5_e), .f(n7_segmentos_5_f), .g(n7_segmentos_5_g));
  _7_segmentos u_7_segmentos_6 (
    .in_1(decoder60_1_unidade), .a(n7_segmentos_6_a), .b(n7_segmentos_6_b), .c(n7_segmentos_6_c),
    .d(n7_segmentos_6_d), .e(n7_segmentos_6_e), .f(n7_segmentos_6_f), .g(n7_segmentos_6_g));
  and and_1 (and_1_out, j_k_ff_2_q[5], j_k_ff_2_q[4], j_k_ff_2_q[3], j_k_ff_2_q[2], ~j_k_ff_2_q[0]);  // AND_Gate
  and and_2 (and_2_out, ~j_k_ff_3_q[5], j_k_ff_3_q[4], j_k_ff_3_q[3], ~j_k_ff_3_q[2], ~j_k_ff_3_q[1], ~j_k_ff_3_q[0]);  // AND_Gate
  Clock clock_1 (.out(clock_1_out));
  and and_3 (and_3_out, j_k_ff_1_q[5], j_k_ff_1_q[4], j_k_ff_1_q[3], j_k_ff_1_q[2], ~j_k_ff_1_q[1], ~j_k_ff_1_q[0]);  // AND_Gate
  J_K_Flip_Flop #(.trigger("falling")) j_k_ff_1 (
    .J(1'b1), .clk(clock_1_out), .K(1'b1), .Q(j_k_ff_1_q[0]), .reset(and_3_out));  // open: Qn, preset, en
  J_K_Flip_Flop #(.trigger("falling")) j_k_ff_2 (
    .J(1'b1), .clk(and_3_out), .K(1'b1), .Q(j_k_ff_2_q[0]), .reset(and_1_out));  // open: Qn, preset, en
  J_K_Flip_Flop #(.trigger("falling")) j_k_ff_3 (
    .J(1'b1), .clk(and_1_out), .K(1'b1), .Q(j_k_ff_3_q[0]), .reset(and_2_out));  // open: Qn, preset, en
  J_K_Flip_Flop #(.trigger("falling")) j_k_ff_4 (
    .J(1'b1), .clk(j_k_ff_1_q[0]), .K(1'b1), .Q(j_k_ff_1_q[1]), .reset(and_3_out));  // open: Qn, preset, en
  decoder60 decoder60_1 (.entrada({1'b0, j_k_ff_1_q}), .dezena(decoder60_1_dezena), .unidade(decoder60_1_unidade));
  J_K_Flip_Flop #(.trigger("falling")) j_k_ff_5 (
    .J(1'b1), .clk(j_k_ff_2_q[0]), .K(1'b1), .Q(j_k_ff_2_q[1]), .reset(and_1_out));  // open: Qn, preset, en
  decoder60 decoder60_2 (.entrada({1'b0, j_k_ff_2_q}), .dezena(decoder60_2_dezena), .unidade(decoder60_2_unidade));
  J_K_Flip_Flop #(.trigger("falling")) j_k_ff_6 (
    .J(1'b1), .clk(j_k_ff_3_q[0]), .K(1'b1), .Q(j_k_ff_3_q[1]), .reset(and_2_out));  // open: Qn, preset, en
  decoder60 decoder60_3 (.entrada({1'b0, j_k_ff_3_q}), .dezena(decoder60_3_dezena), .unidade(decoder60_3_unidade));
  J_K_Flip_Flop #(.trigger("falling")) j_k_ff_7 (
    .J(1'b1), .clk(j_k_ff_1_q[1]), .K(1'b1), .Q(j_k_ff_1_q[2]), .reset(and_3_out));  // open: Qn, preset, en
  J_K_Flip_Flop #(.trigger("falling")) j_k_ff_8 (
    .J(1'b1), .clk(j_k_ff_2_q[1]), .K(1'b1), .Q(j_k_ff_2_q[2]), .reset(and_1_out));  // open: Qn, preset, en
  J_K_Flip_Flop #(.trigger("falling")) j_k_ff_9 (
    .J(1'b1), .clk(j_k_ff_3_q[1]), .K(1'b1), .Q(j_k_ff_3_q[2]), .reset(and_2_out));  // open: Qn, preset, en
  J_K_Flip_Flop #(.trigger("falling")) j_k_ff_10 (
    .J(1'b1), .clk(j_k_ff_1_q[2]), .K(1'b1), .Q(j_k_ff_1_q[3]), .reset(and_3_out));  // open: Qn, preset, en
  J_K_Flip_Flop #(.trigger("falling")) j_k_ff_11 (
    .J(1'b1), .clk(j_k_ff_2_q[2]), .K(1'b1), .Q(j_k_ff_2_q[3]), .reset(and_1_out));  // open: Qn, preset, en
  J_K_Flip_Flop #(.trigger("falling")) j_k_ff_12 (
    .J(1'b1), .clk(j_k_ff_3_q[2]), .K(1'b1), .Q(j_k_ff_3_q[3]), .reset(and_2_out));  // open: Qn, preset, en
  J_K_Flip_Flop #(.trigger("falling")) j_k_ff_13 (
    .J(1'b1), .clk(j_k_ff_1_q[3]), .K(1'b1), .Q(j_k_ff_1_q[4]), .reset(and_3_out));  // open: Qn, preset, en
  J_K_Flip_Flop #(.trigger("falling")) j_k_ff_14 (
    .J(1'b1), .clk(j_k_ff_2_q[3]), .K(1'b1), .Q(j_k_ff_2_q[4]), .reset(and_1_out));  // open: Qn, preset, en
  J_K_Flip_Flop #(.trigger("falling")) j_k_ff_15 (
    .J(1'b1), .clk(j_k_ff_3_q[3]), .K(1'b1), .Q(j_k_ff_3_q[4]), .reset(and_2_out));  // open: Qn, preset, en
  J_K_Flip_Flop #(.trigger("falling")) j_k_ff_16 (
    .J(1'b1), .clk(j_k_ff_1_q[4]), .K(1'b1), .Q(j_k_ff_1_q[5]), .reset(and_3_out));  // open: Qn, preset, en
  J_K_Flip_Flop #(.trigger("falling")) j_k_ff_17 (
    .J(1'b1), .clk(j_k_ff_2_q[4]), .K(1'b1), .Q(j_k_ff_2_q[5]), .reset(and_1_out));  // open: Qn, preset, en
  J_K_Flip_Flop #(.trigger("falling")) j_k_ff_18 (
    .J(1'b1), .clk(j_k_ff_3_q[4]), .K(1'b1), .Q(j_k_ff_3_q[5]), .reset(and_2_out));  // open: Qn, preset, en
endmodule

module decoder60 (
  input  [6:0] entrada,
  output [3:0] dezena,
  output [3:0] unidade
);

  wire [6:4] divider_1_out, divider_1_rem;

  Divider #(.width(7)) divider_1 (
    .a(entrada), .b(7'b0001010), .out({divider_1_out, dezena}), .rem({divider_1_rem, unidade}));  // open: upper
endmodule

module _7_segmentos (
  input  [3:0] in_1,
  output a,
  output b,
  output c,
  output d,
  output e,
  output f,
  output g
);

  wire and_1_out, and_2_out, and_3_out, and_4_out, and_5_out, and_6_out, and_7_out, and_8_out, and_9_out,
       and_10_out, and_11_out, and_12_out, and_13_out, and_14_out, and_15_out, and_16_out, not_1_out,
       not_2_out, not_3_out, not_4_out, not_5_out, not_6_out, not_7_out, not_8_out, not_9_out, not_10_out,
       not_11_out, not_12_out, not_13_out, not_14_out, not_15_out, not_16_out, not_17_out, not_18_out,
       not_19_out, not_20_out, not_21_out;

  not not_1 (not_1_out, in_1[2]);
  not not_2 (not_2_out, in_1[0]);
  not not_3 (not_3_out, in_1[1]);
  not not_4 (not_4_out, in_1[0]);
  not not_5 (not_5_out, in_1[1]);
  not not_6 (not_6_out, in_1[2]);
  not not_7 (not_7_out, in_1[0]);
  not not_8 (not_8_out, in_1[2]);
  not not_9 (not_9_out, in_1[0]);
  not not_10 (not_10_out, in_1[1]);
  not not_11 (not_11_out, in_1[2]);
  not not_12 (not_12_out, in_1[0]);
  not not_13 (not_13_out, in_1[0]);
  not not_14 (not_14_out, in_1[1]);
  not not_15 (not_15_out, in_1[0]);
  not not_16 (not_16_out, in_1[1]);
  not not_17 (not_17_out, in_1[0]);
  not not_18 (not_18_out, in_1[2]);
  not not_19 (not_19_out, in_1[1]);
  not not_20 (not_20_out, in_1[0]);
  and and_1 (and_1_out, not_1_out, not_2_out);
  and and_2 (and_2_out, in_1[2], in_1[0]);
  not not_21 (not_21_out, in_1[2]);
  and and_3 (and_3_out, not_3_out, not_4_out);
  and and_4 (and_4_out, in_1[1], in_1[0]);
  or or_1 (c, not_5_out, in_1[0], in_1[2]);
  and and_5 (and_5_out, not_6_out, not_7_out);
  and and_6 (and_6_out, not_8_out, in_1[1]);
  and and_7 (and_7_out, in_1[1], not_9_out);
  and and_8 (and_8_out, in_1[2], not_10_out, in_1[0]);
  and and_9 (and_9_out, not_11_out, not_12_out);
  and and_10 (and_10_out, in_1[1], not_13_out);
  and and_11 (and_11_out, not_14_out, not_15_out);
  and and_12 (and_12_out, in_1[2], not_16_out);
  and and_13 (and_13_out, in_1[2], not_17_out);
  and and_14 (and_14_out, not_18_out, in_1[1]);
  and and_15 (and_15_out, in_1[2], not_19_out);
  and and_16 (and_16_out, in_1[2], not_20_out);
  or or_2 (a, and_1_out, in_1[1], and_2_out, in_1[3]);
  or or_3 (b, not_21_out, and_3_out, and_4_out);
  or or_4 (d, and_5_out, and_6_out, and_7_out, and_8_out, in_1[3]);
  or or_5 (e, and_9_out, and_10_out);
  or or_6 (f, and_11_out, and_12_out, and_13_out, in_1[3]);
  or or_7 (g, and_14_out, and_15_out, and_16_out, in_1[3]);
endmodule
