// Logisim project Tempotizador .circ as structural Verilog: 5 circuits, main circuit Relogio
module main (
);

  wire and_1_out, and_2_out, and_3_out, and_4_out, and_5_out, and_6_out, and_7_out, and_8_out, clock_1_out,
       clock_2_out, clock_3_out, clock_4_out, clock_5_out, clock_6_out, clock_7_out, j_k_ff_17_q,
       j_k_ff_18_q, j_k_ff_19_q, j_k_ff_20_q, j_k_ff_21_q, j_k_ff_22_q, j_k_ff_25_q, j_k_ff_26_q;
  wire [3:0] j_k_ff_1_q, j_k_ff_2_q, j_k_ff_3_q, j_k_ff_4_q, j_k_ff_17_qn, j_k_ff_18_qn, j_k_ff_23_q,
       j_k_ff_24_q;

  Clock clock_1 (.out(clock_1_out));
  Hex_Digit_Display hex_digit_display_1 (.value(j_k_ff_1_q));  // open: dp
  and and_1 (and_1_out, j_k_ff_1_q[0], ~j_k_ff_1_q[1], ~j_k_ff_1_q[2], j_k_ff_1_q[3]);  // AND_Gate
  Clock clock_2 (.out(clock_2_out));
  Hex_Digit_Display hex_digit_display_2 (.value(j_k_ff_2_q));  // open: dp
  and and_2 (and_2_out, j_k_ff_2_q[0], ~j_k_ff_2_q[1], ~j_k_ff_2_q[2], ~j_k_ff_2_q[3]);  // AND_Gate
  Clock clock_3 (.out(clock_3_out));
  Hex_Digit_Display hex_digit_display_3 (.value(j_k_ff_3_q));  // open: dp
  and and_3 (and_3_out, ~j_k_ff_3_q[0], j_k_ff_3_q[1], j_k_ff_3_q[2], ~j_k_ff_3_q[3]);  // AND_Gate
  Clock clock_4 (.out(clock_4_out));
  Hex_Digit_Display hex_digit_display_4 (.value(j_k_ff_4_q));  // open: dp
  and and_4 (and_4_out, ~j_k_ff_4_q[0], j_k_ff_4_q[1], ~j_k_ff_4_q[2], j_k_ff_4_q[3]);  // AND_Gate
  J_K_Flip_Flop #(.trigger("falling")) j_k_ff_1 (
    .J(1'b1), .clk(clock_1_out), .K(1'b1), .Q(j_k_ff_1_q[0]), .reset(and_1_out));  // open: Qn, preset, en
  J_K_Flip_Flop j_k_ff_2 (
    .J(1'b1), .clk(clock_2_out), .K(1'b1), .Q(j_k_ff_2_q[0]), .reset(and_2_out));  // open: Qn, preset, en
  J_K_Flip_Flop #(.trigger("falling")) j_k_ff_3 (
    .J(1'b1), .clk(clock_3_out), .K(1'b1), .Q(j_k_ff_3_q[0]), .reset(and_3_out));  // open: Qn, preset, en
  J_K_Flip_Flop #(.trigger("falling")) j_k_ff_4 (
    .J(1'b1), .clk(clock_4_out), .K(1'b1), .Q(j_k_ff_4_q[0]), .reset(and_4_out));  // open: Qn, preset, en
  J_K_Flip_Flop #(.trigger("falling")) j_k_ff_5 (
    .J(1'b1), .clk(j_k_ff_1_q[0]), .K(1'b1), .Q(j_k_ff_1_q[1]), .preset(and_1_out));  // open: Qn, en, reset
  J_K_Flip_Flop j_k_ff_6 (
    .J(1'b1), .clk(j_k_ff_2_q[0]), .K(1'b1), .Q(j_k_ff_2_q[1]), .reset(and_2_out));  // open: Qn, preset, en
  J_K_Flip_Flop #(.trigger("falling")) j_k_ff_7 (
    .J(1'b1), .clk(j_k_ff_3_q[0]), .K(1'b1), .Q(j_k_ff_3_q[1]), .reset(and_3_out));  // open: Qn, preset, en
  J_K_Flip_Flop #(.trigger("falling")) j_k_ff_8 (
    .J(1'b1), .clk(j_k_ff_4_q[0]), .K(1'b1), .Q(j_k_ff_4_q[1]), .reset(and_4_out));  // open: Qn, preset, en
  J_K_Flip_Flop #(.trigger("falling")) j_k_ff_9 (
    .J(1'b1), .clk(j_k_ff_1_q[1]), .K(1'b1), .Q(j_k_ff_1_q[2]), .reset(and_1_out));  // open: Qn, preset, en
  J_K_Flip_Flop j_k_ff_10 (
    .J(1'b1), .clk(j_k_ff_2_q[1]), .K(1'b1), .Q(j_k_ff_2_q[2]), .reset(and_2_out));  // open: Qn, preset, en
  J_K_Flip_Flop #(.trigger("falling")) j_k_ff_11 (
    .J(1'b1), .clk(j_k_ff_3_q[1]), .K(1'b1), .Q(j_k_ff_3_q[2]), .reset(and_3_out));  // open: Qn, preset, en
  J_K_Flip_Flop #(.trigger("falling")) j_k_ff_12 (
    .J(1'b1), .clk(j_k_ff_4_q[1]), .K(1'b1), .Q(j_k_ff_4_q[2]), .reset(and_4_out));  // open: Qn, preset, en
  J_K_Flip_Flop #(.trigger("falling")) j_k_ff_13 (
    .J(1'b1), .clk(j_k_ff_1_q[2]), .K(1'b1), .Q(j_k_ff_1_q[3]), .reset(and_1_out));  // open: Qn, preset, en
  J_K_Flip_Flop j_k_ff_14 (
    .J(1'b1), .clk(j_k_ff_2_q[2]), .K(1'b1), .Q(j_k_ff_2_q[3]), .preset(and_2_out));  // open: Qn, en, reset
  J_K_Flip_Flop #(.trigger("falling")) j_k_ff_15 (
    .J(1'b1), .clk(j_k_ff_3_q[2]), .K(1'b1), .Q(j_k_ff_3_q[3]), .reset(and_3_out));  // open: Qn, preset, en
  J_K_Flip_Flop #(.trigger("falling")) j_k_ff_16 (
    .J(1'b1), .clk(j_k_ff_4_q[2]), .K(1'b1), .Q(j_k_ff_4_q[3]), .reset(and_4_out));  // open: Qn, preset, en
  Clock clock_5 (.out(clock_5_out));
  Hex_Digit_Display hex_digit_display_5 (.value(j_k_ff_17_qn));  // open: dp
  Clock clock_6 (.out(clock_6_out));
  Hex_Digit_Display hex_digit_display_6 (.value(j_k_ff_18_qn));  // open: dp
  Hex_Digit_Display hex_digit_display_7 (.value(j_k_ff_24_q));  // open: dp
  Hex_Digit_Display hex_digit_display_8 (.value(j_k_ff_23_q));  // open: dp
  J_K_Flip_Flop j_k_ff_17 (
    .J(1'b1), .clk(clock_5_out), .K(1'b1), .Q(j_k_ff_17_q), .Qn(j_k_ff_17_qn[0]), .reset(and_5_out));  // open: preset, en
  and and_5 (and_5_out, ~j_k_ff_17_qn[0], j_k_ff_17_qn[1], ~j_k_ff_17_qn[2], j_k_ff_17_qn[3]);  // AND_Gate
  J_K_Flip_Flop #(.trigger("falling")) j_k_ff_18 (
    .J(1'b1), .clk(clock_6_out), .K(1'b1), .Q(j_k_ff_18_q), .Qn(j_k_ff_18_qn[0]), .reset(and_6_out));  // open: preset, en
  and and_6 (and_6_out, j_k_ff_18_qn[0], j_k_ff_18_qn[1], j_k_ff_18_qn[2], j_k_ff_18_qn[3]);
  J_K_Flip_Flop j_k_ff_19 (
    .J(1'b1), .clk(j_k_ff_17_q), .K(1'b1), .Q(j_k_ff_19_q), .Qn(j_k_ff_17_qn[1]), .reset(and_5_out));  // open: preset, en
  J_K_Flip_Flop #(.trigger("falling")) j_k_ff_20 (
    .J(1'b1), .clk(j_k_ff_18_q), .K(1'b1), .Q(j_k_ff_20_q), .Qn(j_k_ff_18_qn[1]), .preset(and_6_out));  // open: en, reset
  Clock clock_7 (.out(clock_7_out));
  and and_7 (and_7_out, ~j_k_ff_23_q[0], j_k_ff_23_q[1], ~j_k_ff_23_q[2], j_k_ff_23_q[3]);  // AND_Gate
  and and_8 (and_8_out, ~j_k_ff_24_q[0], j_k_ff_24_q[1], j_k_ff_24_q[2], ~j_k_ff_24_q[3]);  // AND_Gate
  J_K_Flip_Flop j_k_ff_21 (
    .J(1'b1), .clk(j_k_ff_19_q), .K(1'b1), .Q(j_k_ff_21_q), .Qn(j_k_ff_17_qn[2]), .reset(and_5_out));  // open: preset, en
  J_K_Flip_Flop #(.trigger("falling")) j_k_ff_22 (
    .J(1'b1), .clk(j_k_ff_20_q), .K(1'b1), .Q(j_k_ff_22_q), .Qn(j_k_ff_18_qn[2]), .reset(and_6_out));  // open: preset, en
  J_K_Flip_Flop #(.trigger("falling")) j_k_ff_23 (
    .J(1'b1), .clk(clock_7_out), .K(1'b1), .Q(j_k_ff_23_q[0]), .reset(and_7_out));  // open: Qn, preset, en
  J_K_Flip_Flop #(.trigger("falling")) j_k_ff_24 (
    .J(1'b1), .clk(j_k_ff_23_q[3]), .K(1'b1), .Q(j_k_ff_24_q[0]), .reset(and_8_out));  // open: Qn, preset, en
  J_K_Flip_Flop j_k_ff_25 (
    .J(1'b1), .clk(j_k_ff_21_q), .K(1'b1), .Q(j_k_ff_25_q), .Qn(j_k_ff_17_qn[3]), .reset(and_5_out));  // open: preset, en
  J_K_Flip_Flop #(.trigger("falling")) j_k_ff_26 (
    .J(1'b1), .clk(j_k_ff_22_q), .K(1'b1), .Q(j_k_ff_26_q), .Qn(j_k_ff_18_qn[3]), .reset(and_6_out));  // open: preset, en
  J_K_Flip_Flop #(.trigger("falling")) j_k_ff_27 (
    .J(1'b1), .clk(j_k_ff_23_q[0]), .K(1'b1), .Q(j_k_ff_23_q[1]), .reset(and_7_out));  // open: Qn, preset, en
  J_K_Flip_Flop #(.trigger("falling")) j_k_ff_28 (
    .J(1'b1), .clk(j_k_ff_24_q[0]), .K(1'b1), .Q(j_k_ff_24_q[1]), .reset(and_8_out));  // open: Qn, preset, en
  J_K_Flip_Flop #(.trigger("falling")) j_k_ff_29 (
    .J(1'b1), .clk(j_k_ff_23_q[1]), .K(1'b1), .Q(j_k_ff_23_q[2]), .reset(and_7_out));  // open: Qn, preset, en
  J_K_Flip_Flop #(.trigger("falling")) j_k_ff_30 (
    .J(1'b1), .clk(j_k_ff_24_q[1]), .K(1'b1), .Q(j_k_ff_24_q[2]), .reset(and_8_out));  // open: Qn, preset, en
  J_K_Flip_Flop #(.trigger("falling")) j_k_ff_31 (
    .J(1'b1), .clk(j_k_ff_23_q[2]), .K(1'b1), .Q(j_k_ff_23_q[3]), .reset(and_7_out));  // open: Qn, preset, en
  J_K_Flip_Flop #(.trigger("falling")) j_k_ff_32 (
    .J(1'b1), .clk(j_k_ff_24_q[2]), .K(1'b1), .Q(j_k_ff_24_q[3]), .reset(and_8_out));  // open: Qn, preset, en
endmodule

module _7segmentos (
  input  [3:0] b3,
  output a,
  output b,
  output c,
  output d,
  output e,
  output f,
  output g
);

  wire and_1_out, and_2_out, and_3_out, and_4_out, and_5_out, and_6_out, and_7_out, and_8_out, and_9_out,
       and_10_out, and_11_out, and_12_out, and_13_out, and_14_out, and_15_out, and_16_out, not_1_out,
       not_2_out, not_3_out, not_4_out, not_5_out, not_6_out, not_7_out, not_8_out, not_9_out, not_10_out,
       not_11_out, not_12_out, not_13_out, not_14_out, not_15_out, not_16_out, not_17_out, not_18_out,
       not_19_out, not_20_out, not_21_out;

  not not_1 (not_1_out, b3[2]);
  not not_2 (not_2_out, b3[0]);
  not not_3 (not_3_out, b3[1]);
  not not_4 (not_4_out, b3[0]);
  not not_5 (not_5_out, b3[1]);
  not not_6 (not_6_out, b3[2]);
  not not_7 (not_7_out, b3[0]);
  not not_8 (not_8_out, b3[2]);
  not not_9 (not_9_out, b3[0]);
  not not_10 (not_10_out, b3[1]);
  not not_11 (not_11_out, b3[2]);
  not not_12 (not_12_out, b3[0]);
  not not_13 (not_13_out, b3[0]);
  not not_14 (not_14_out, b3[1]);
  not not_15 (not_15_out, b3[0]);
  not not_16 (not_16_out, b3[1]);
  not not_17 (not_17_out, b3[0]);
  not not_18 (not_18_out, b3[2]);
  not not_19 (not_19_out, b3[1]);
  not not_20 (not_20_out, b3[0]);
  and and_1 (and_1_out, not_1_out, not_2_out);
  and and_2 (and_2_out, b3[2], b3[0]);
  not not_21 (not_21_out, b3[2]);
  and and_3 (and_3_out, not_3_out, not_4_out);
  and and_4 (and_4_out, b3[1], b3[0]);
  or or_1 (c, not_5_out, b3[0], b3[2]);
  and and_5 (and_5_out, not_6_out, not_7_out);
  and and_6 (and_6_out, not_8_out, b3[1]);
  and and_7 (and_7_out, b3[1], not_9_out);
  and and_8 (and_8_out, b3[2], not_10_out, b3[0]);
  and and_9 (and_9_out, not_11_out, not_12_out);
  and and_10 (and_10_out, b3[1], not_13_out);
  and and_11 (and_11_out, not_14_out, not_15_out);
  and and_12 (and_12_out, b3[2], not_16_out);
  and and_13 (and_13_out, b3[2], not_17_out);
  and and_14 (and_14_out, not_18_out, b3[1]);
  and and_15 (and_15_out, b3[2], not_19_out);
  and and_16 (and_16_out, b3[2], not_20_out);
  or or_2 (a, and_1_out, b3[1], and_2_out, b3[3]);
  or or_3 (b, not_21_out, and_3_out, and_4_out);
  or or_4 (d, and_5_out, and_6_out, and_7_out, and_8_out, b3[3]);
  or or_5 (e, and_9_out, and_10_out);
  or or_6 (f, and_11_out, and_12_out, and_13_out, b3[3]);
  or or_7 (g, and_14_out, and_15_out, and_16_out, b3[3]);
endmodule

module Relogio (
);

  wire and_1_out, and_3_out, and_4_out, and_5_out, and_6_out, and_7_out, and_8_out, clock_1_out,
       n7segmentos_1_a, n7segmentos_1_b, n7segmentos_1_c, n7segmentos_1_d, n7segmentos_1_e, n7segmentos_1_f,
       n7segmentos_1_g, n7segmentos_2_a, n7segmentos_2_b, n7segmentos_2_c, n7segmentos_2_d, n7segmentos_2_e,
       n7segmentos_2_f, n7segmentos_2_g, n7segmentos_3_a, n7segmentos_3_b, n7segmentos_3_c, n7segmentos_3_d,
       n7segmentos_3_e, n7segmentos_3_f, n7segmentos_3_g, n7segmentos_4_a, n7segmentos_4_b, n7segmentos_4_c,
       n7segmentos_4_d, n7segmentos_4_e, n7segmentos_4_f, n7segmentos_4_g, n7segmentos_5_a, n7segmentos_5_b,
       n7segmentos_5_c, n7segmentos_5_d, n7segmentos_5_e, n7segmentos_5_f, n7segmentos_5_g, n7segmentos_6_a,
       n7segmentos_6_b, n7segmentos_6_c, n7segmentos_6_d, n7segmentos_6_e, n7segmentos_6_f, n7segmentos_6_g;
  wire [3:0] j_k_ff_1_q, j_k_ff_2_q, j_k_ff_3_q, j_k_ff_4_q, j_k_ff_5_q, j_k_ff_6_q;

  _7_Segment_Display u_7_segment_display_1 (
    .g(n7segmentos_2_g), .f(n7segmentos_2_f), .a(n7segmentos_2_a), .b(n7segmentos_2_b), .e(n7segmentos_2_e),
    .d(n7segmentos_2_d), .c(n7segmentos_2_c));  // open: dp
  _7_Segment_Display u_7_segment_display_2 (
    .g(n7segmentos_1_g), .f(n7segmentos_1_f), .a(n7segmentos_1_a), .b(n7segmentos_1_b), .e(n7segmentos_1_e),
    .d(n7segmentos_1_d), .c(n7segmentos_1_c));  // open: dp
  _7segmentos u_7segmentos_1 (
    .b3(j_k_ff_5_q), .a(n7segmentos_1_a), .b(n7segmentos_1_b), .c(n7segmentos_1_c), .d(n7segmentos_1_d),
    .e(n7segmentos_1_e), .f(n7segmentos_1_f), .g(n7segmentos_1_g));
  _7segmentos u_7segmentos_2 (
    .b3(j_k_ff_6_q), .a(n7segmentos_2_a), .b(n7segmentos_2_b), .c(n7segmentos_2_c), .d(n7segmentos_2_d),
    .e(n7segmentos_2_e), .f(n7segmentos_2_f), .g(n7segmentos_2_g));
  _7_Segment_Display u_7_segment_display_3 (
    .g(n7segmentos_4_g), .f(n7segmentos_4_f), .a(n7segmentos_4_a), .b(n7segmentos_4_b), .e(n7segmentos_4_e),
    .d(n7segmentos_4_d), .c(n7segmentos_4_c));  // open: dp
  _7_Segment_Display u_7_segment_display_4 (
    .g(n7segmentos_3_g), .f(n7segmentos_3_f), .a(n7segmentos_3_a), .b(n7segmentos_3_b), .e(n7segmentos_3_e),
    .d(n7segmentos_3_d), .c(n7segmentos_3_c));  // open: dp
  _7segmentos u_7segmentos_3 (
    .b3(j_k_ff_4_q), .a(n7segmentos_3_a), .b(n7segmentos_3_b), .c(n7segmentos_3_c), .d(n7segmentos_3_d),
    .e(n7segmentos_3_e), .f(n7segmentos_3_f), .g(n7segmentos_3_g));
  _7_Segment_Display u_7_segment_display_5 (
    .g(n7segmentos_6_g), .f(n7segmentos_6_f), .a(n7segmentos_6_a), .b(n7segmentos_6_b), .e(n7segmentos_6_e),
    .d(n7segmentos_6_d), .c(n7segmentos_6_c));  // open: dp
  _7segmentos u_7segmentos_4 (
    .b3(j_k_ff_3_q), .a(n7segmentos_4_a), .b(n7segmentos_4_b), .c(n7segmentos_4_c), .d(n7segmentos_4_d),
    .e(n7segmentos_4_e), .f(n7segmentos_4_f), .g(n7segmentos_4_g));
  _7_Segment_Display u_7_segment_display_6 (
    .g(n7segmentos_5_g), .f(n7segmentos_5_f), .a(n7segmentos_5_a), .b(n7segmentos_5_b), .e(n7segmentos_5_e),
    .d(n7segmentos_5_d), .c(n7segmentos_5_c));  // open: dp
  _7segmentos u_7segmentos_5 (
    .b3(j_k_ff_1_q), .a(n7segmentos_5_a), .b(n7segmentos_5_b), .c(n7segmentos_5_c), .d(n7segmentos_5_d),
    .e(n7segmentos_5_e), .f(n7segmentos_5_f), .g(n7segmentos_5_g));
  _7segmentos u_7segmentos_6 (
    .b3(j_k_ff_2_q), .a(n7segmentos_6_a), .b(n7segmentos_6_b), .c(n7segmentos_6_c), .d(n7segmentos_6_d),
    .e(n7segmentos_6_e), .f(n7segmentos_6_f), .g(n7segmentos_6_g));
  and and_1 (and_1_out, ~j_k_ff_5_q[0], ~j_k_ff_5_q[1], j_k_ff_5_q[2], ~j_k_ff_5_q[3]);  // AND_Gate
  // AND_Gate and_2 has open pins: in0=and_1_out, out=open
  Clock clock_1 (.out(clock_1_out));
  and and_3 (and_3_out, ~j_k_ff_1_q[0], j_k_ff_1_q[1], ~j_k_ff_1_q[2], j_k_ff_1_q[3]);  // AND_Gate
  and and_4 (and_4_out, ~j_k_ff_2_q[0], j_k_ff_2_q[1], j_k_ff_2_q[2], ~j_k_ff_2_q[3]);  // AND_Gate
  and and_5 (and_5_out, ~j_k_ff_3_q[0], j_k_ff_3_q[1], ~j_k_ff_3_q[2], j_k_ff_3_q[3]);  // AND_Gate
  and and_6 (and_6_out, ~j_k_ff_4_q[0], j_k_ff_4_q[1], j_k_ff_4_q[2], ~j_k_ff_4_q[3]);  // AND_Gate
  and and_7 (and_7_out, ~j_k_ff_5_q[0], j_k_ff_5_q[1], ~j_k_ff_5_q[2], j_k_ff_5_q[3]);  // AND_Gate
  and and_8 (and_8_out, j_k_ff_6_q[0], j_k_ff_6_q[1], ~j_k_ff_6_q[2], ~j_k_ff_6_q[3]);  // AND_Gate
  J_K_Flip_Flop #(.trigger("falling")) j_k_ff_1 (
    .J(1'b1), .clk(clock_1_out), .K(1'b1), .Q(j_k_ff_1_q[0]), .reset(and_3_out));  // open: Qn, preset, en
  J_K_Flip_Flop #(.trigger("falling")) j_k_ff_2 (
    .J(1'b1), .clk(j_k_ff_1_q[3]), .K(1'b1), .Q(j_k_ff_2_q[0]), .reset(and_4_out));  // open: Qn, preset, en
  J_K_Flip_Flop #(.trigger("falling")) j_k_ff_3 (
    .J(1'b1), .clk(and_4_out), .K(1'b1), .Q(j_k_ff_3_q[0]), .reset(and_5_out));  // open: Qn, preset, en
  J_K_Flip_Flop #(.trigger("falling")) j_k_ff_4 (
    .J(1'b1), .clk(j_k_ff_3_q[3]), .K(1'b1), .Q(j_k_ff_4_q[0]), .reset(and_6_out));  // open: Qn, preset, en
  J_K_Flip_Flop #(.trigger("falling")) j_k_ff_5 (
    .J(1'b1), .clk(and_6_out), .K(1'b1), .Q(j_k_ff_5_q[0]), .reset(and_7_out));  // open: Qn, preset, en
  J_K_Flip_Flop #(.trigger("falling")) j_k_ff_6 (
    .J(1'b1), .clk(j_k_ff_5_q[3]), .K(1'b1), .Q(j_k_ff_6_q[0]), .reset(and_8_out));  // open: Qn, preset, en
  J_K_Flip_Flop #(.trigger("falling")) j_k_ff_7 (
    .J(1'b1), .clk(j_k_ff_1_q[0]), .K(1'b1), .Q(j_k_ff_1_q[1]), .reset(and_3_out));  // open: Qn, preset, en
  J_K_Flip_Flop #(.trigger("falling")) j_k_ff_8 (
    .J(1'b1), .clk(j_k_ff_2_q[0]), .K(1'b1), .Q(j_k_ff_2_q[1]), .reset(and_4_out));  // open: Qn, preset, en
  J_K_Flip_Flop #(.trigger("falling")) j_k_ff_9 (
    .J(1'b1), .clk(j_k_ff_3_q[0]), .K(1'b1), .Q(j_k_ff_3_q[1]), .reset(and_5_out));  // open: Qn, preset, en
  J_K_Flip_Flop #(.trigger("falling")) j_k_ff_10 (
    .J(1'b1), .clk(j_k_ff_4_q[0]), .K(1'b1), .Q(j_k_ff_4_q[1]), .reset(and_6_out));  // open: Qn, preset, en
  J_K_Flip_Flop #(.trigger("falling")) j_k_ff_11 (
    .J(1'b1), .clk(j_k_ff_5_q[0]), .K(1'b1), .Q(j_k_ff_5_q[1]), .reset(and_7_out));  // open: Qn, preset, en
  J_K_Flip_Flop #(.trigger("falling")) j_k_ff_12 (
    .J(1'b1), .clk(j_k_ff_6_q[0]), .K(1'b1), .Q(j_k_ff_6_q[1]), .reset(and_8_out));  // open: Qn, preset, en
  J_K_Flip_Flop #(.trigger("falling")) j_k_ff_13 (
    .J(1'b1), .clk(j_k_ff_1_q[1]), .K(1'b1), .Q(j_k_ff_1_q[2]), .reset(and_3_out));  // open: Qn, preset, en
  J_K_Flip_Flop #(.trigger("falling")) j_k_ff_14 (
    .J(1'b1), .clk(j_k_ff_2_q[1]), .K(1'b1), .Q(j_k_ff_2_q[2]), .reset(and_4_out));  // open: Qn, preset, en
  J_K_Flip_Flop #(.trigger("falling")) j_k_ff_15 (
    .J(1'b1), .clk(j_k_ff_3_q[1]), .K(1'b1), .Q(j_k_ff_3_q[2]), .reset(and_5_out));  // open: Qn, preset, en
  J_K_Flip_Flop #(.trigger("falling")) j_k_ff_16 (
    .J(1'b1), .clk(j_k_ff_4_q[1]), .K(1'b1), .Q(j_k_ff_4_q[2]), .reset(and_6_out));  // open: Qn, preset, en
  J_K_Flip_Flop #(.trigger("falling")) j_k_ff_17 (
    .J(1'b1), .clk(j_k_ff_5_q[1]), .K(1'b1), .Q(j_k_ff_5_q[2]), .reset(and_7_out));  // open: Qn, preset, en
  J_K_Flip_Flop #(.trigger("falling")) j_k_ff_18 (
    .J(1'b1), .clk(j_k_ff_6_q[1]), .K(1'b1), .Q(j_k_ff_6_q[2]), .reset(and_8_out));  // open: Qn, preset, en
  J_K_Flip_Flop #(.trigger("falling")) j_k_ff_19 (
    .J(1'b1), .clk(j_k_ff_1_q[2]), .K(1'b1), .Q(j_k_ff_1_q[3]), .reset(and_3_out));  // open: Qn, preset, en
  J_K_Flip_Flop #(.trigger("falling")) j_k_ff_20 (
    .J(1'b1), .clk(j_k_ff_2_q[2]), .K(1'b1), .Q(j_k_ff_2_q[3]), .reset(and_4_out));  // open: Qn, preset, en
  J_K_Flip_Flop #(.trigger("falling")) j_k_ff_21 (
    .J(1'b1), .clk(j_k_ff_3_q[2]), .K(1'b1), .Q(j_k_ff_3_q[3]), .reset(and_5_out));  // open: Qn, preset, en
  J_K_Flip_Flop #(.trigger("falling")) j_k_ff_22 (
    .J(1'b1), .clk(j_k_ff_4_q[2]), .K(1'b1), .Q(j_k_ff_4_q[3]), .reset(and_6_out));  // open: Qn, preset, en
  J_K_Flip_Flop #(.trigger("falling")) j_k_ff_23 (
    .J(1'b1), .clk(j_k_ff_5_q[2]), .K(1'b1), .Q(j_k_ff_5_q[3]), .reset(and_7_out));  // open: Qn, preset, en
  J_K_Flip_Flop #(.trigger("falling")) j_k_ff_24 (
    .J(1'b1), .clk(j_k_ff_6_q[2]), .K(1'b1), .Q(j_k_ff_6_q[3]), .reset(and_8_out));  // open: Qn, preset, en
endmodule

module decoder (
  input  [6:0] in_1,
  output [3:0] Dezena,
  output [3:0] Unidade
);

  wire [6:4] divider_1_out, divider_1_rem;

  Divider #(.width(7)) divider_1 (
    .a(in_1), .b(7'b0001010), .out({divider_1_out, Dezena}), .rem({divider_1_rem, Unidade}));  // open: upper
endmodule

module Relogio24h (
);

  wire and_1_out, and_2_out, clock_1_out, clock_2_out, n7segmentos_1_a, n7segmentos_1_b, n7segmentos_1_c,
       n7segmentos_1_d, n7segmentos_1_e, n7segmentos_1_f, n7segmentos_1_g, n7segmentos_2_a, n7segmentos_2_b,
       n7segmentos_2_c, n7segmentos_2_d, n7segmentos_2_e, n7segmentos_2_f, n7segmentos_2_g, n7segmentos_3_a,
       n7segmentos_3_b, n7segmentos_3_c, n7segmentos_3_d, n7segmentos_3_e, n7segmentos_3_f, n7segmentos_3_g,
       n7segmentos_4_a, n7segmentos_4_b, n7segmentos_4_c, n7segmentos_4_d, n7segmentos_4_e, n7segmentos_4_f,
       n7segmentos_4_g, n7segmentos_5_a, n7segmentos_5_b, n7segmentos_5_c, n7segmentos_5_d, n7segmentos_5_e,
       n7segmentos_5_f, n7segmentos_5_g, n7segmentos_6_a, n7segmentos_6_b, n7segmentos_6_c, n7segmentos_6_d,
       n7segmentos_6_e, n7segmentos_6_f, n7segmentos_6_g;
  wire [3:0] decoder_1_dezena, decoder_1_unidade, decoder_2_dezena, decoder_2_unidade, undriven, undriven_2,
       undriven_3, undriven_4;
  wire [5:0] j_k_ff_1_q, j_k_ff_2_q;

  _7_Segment_Display u_7_segment_display_1 (
    .g(n7segmentos_2_g), .f(n7segmentos_2_f), .a(n7segmentos_2_a), .b(n7segmentos_2_b), .e(n7segmentos_2_e),
    .d(n7segmentos_2_d), .c(n7segmentos_2_c));  // open: dp
  _7_Segment_Display u_7_segment_display_2 (
    .g(n7segmentos_1_g), .f(n7segmentos_1_f), .a(n7segmentos_1_a), .b(n7segmentos_1_b), .e(n7segmentos_1_e),
    .d(n7segmentos_1_d), .c(n7segmentos_1_c));  // open: dp
  _7segmentos u_7segmentos_1 (
    .b3(undriven_2), .a(n7segmentos_1_a), .b(n7segmentos_1_b), .c(n7segmentos_1_c), .d(n7segmentos_1_d),
    .e(n7segmentos_1_e), .f(n7segmentos_1_f), .g(n7segmentos_1_g));
  _7segmentos u_7segmentos_2 (
    .b3(undriven), .a(n7segmentos_2_a), .b(n7segmentos_2_b), .c(n7segmentos_2_c), .d(n7segmentos_2_d),
    .e(n7segmentos_2_e), .f(n7segmentos_2_f), .g(n7segmentos_2_g));
  _7_Segment_Display u_7_segment_display_3 (
    .g(n7segmentos_3_g), .f(n7segmentos_3_f), .a(n7segmentos_3_a), .b(n7segmentos_3_b), .e(n7segmentos_3_e),
    .d(n7segmentos_3_d), .c(n7segmentos_3_c));  // open: dp
  _7_Segment_Display u_7_segment_display_4 (
    .g(n7segmentos_4_g), .f(n7segmentos_4_f), .a(n7segmentos_4_a), .b(n7segmentos_4_b), .e(n7segmentos_4_e),
    .d(n7segmentos_4_d), .c(n7segmentos_4_c));  // open: dp
  _7segmentos u_7segmentos_3 (
    .b3(undriven_3), .a(n7segmentos_3_a), .b(n7segmentos_3_b), .c(n7segmentos_3_c), .d(n7segmentos_3_d),
    .e(n7segmentos_3_e), .f(n7segmentos_3_f), .g(n7segmentos_3_g));
  _7_Segment_Display u_7_segment_display_5 (
    .g(n7segmentos_5_g), .f(n7segmentos_5_f), .a(n7segmentos_5_a), .b(n7segmentos_5_b), .e(n7segmentos_5_e),
    .d(n7segmentos_5_d), .c(n7segmentos_5_c));  // open: dp
  _7segmentos u_7segmentos_4 (
    .b3(undriven_4), .a(n7segmentos_4_a), .b(n7segmentos_4_b), .c(n7segmentos_4_c), .d(n7segmentos_4_d),
    .e(n7segmentos_4_e), .f(n7segmentos_4_f), .g(n7segmentos_4_g));
  _7_Segment_Display u_7_segment_display_6 (
    .g(n7segmentos_6_g), .f(n7segmentos_6_f), .a(n7segmentos_6_a), .b(n7segmentos_6_b), .e(n7segmentos_6_e),
    .d(n7segmentos_6_d), .c(n7segmentos_6_c));  // open: dp
  _7segmentos u_7segmentos_5 (
    .b3(decoder_1_dezena), .a(n7segmentos_5_a), .b(n7segmentos_5_b), .c(n7segmentos_5_c),
    .d(n7segmentos_5_d), .e(n7segmentos_5_e), .f(n7segmentos_5_f), .g(n7segmentos_5_g));
  _7segmentos u_7segmentos_6 (
    .b3(decoder_1_unidade), .a(n7segmentos_6_a), .b(n7segmentos_6_b), .c(n7segmentos_6_c),
    .d(n7segmentos_6_d), .e(n7segmentos_6_e), .f(n7segmentos_6_f), .g(n7segmentos_6_g));
  Clock clock_1 (.out(clock_1_out));
  and and_1 (and_1_out, j_k_ff_1_q[5], j_k_ff_1_q[4], j_k_ff_1_q[3], j_k_ff_1_q[2], ~j_k_ff_1_q[1], ~j_k_ff_1_q[0]);  // AND_Gate
  Clock clock_2 (.out(clock_2_out));
  and and_2 (and_2_out, j_k_ff_2_q[5], j_k_ff_2_q[4], j_k_ff_2_q[3], j_k_ff_2_q[2], ~j_k_ff_2_q[1], ~j_k_ff_2_q[0]);  // AND_Gate
  J_K_Flip_Flop #(.trigger("falling")) j_k_ff_1 (
    .J(1'b1), .clk(clock_1_out), .K(1'b1), .Q(j_k_ff_1_q[0]), .reset(and_1_out));  // open: Qn, preset, en
  decoder decoder_1 (.in_1({1'b0, j_k_ff_1_q}), .Dezena(decoder_1_dezena), .Unidade(decoder_1_unidade));
  J_K_Flip_Flop #(.trigger("falling")) j_k_ff_2 (
    .J(1'b1), .clk(clock_2_out), .K(1'b1), .Q(j_k_ff_2_q[0]), .reset(and_2_out));  // open: Qn, preset, en
  decoder decoder_2 (.in_1({1'b0, j_k_ff_2_q}), .Dezena(decoder_2_dezena), .Unidade(decoder_2_unidade));
  J_K_Flip_Flop #(.trigger("falling")) j_k_ff_3 (
    .J(1'b1), .clk(j_k_ff_1_q[0]), .K(1'b1), .Q(j_k_ff_1_q[1]), .reset(and_1_out));  // open: Qn, preset, en
  J_K_Flip_Flop #(.trigger("falling")) j_k_ff_4 (
    .J(1'b1), .clk(j_k_ff_2_q[0]), .K(1'b1), .Q(j_k_ff_2_q[1]), .reset(and_2_out));  // open: Qn, preset, en
  J_K_Flip_Flop #(.trigger("falling")) j_k_ff_5 (
    .J(1'b1), .clk(j_k_ff_1_q[1]), .K(1'b1), .Q(j_k_ff_1_q[2]), .reset(and_1_out));  // open: Qn, preset, en
  J_K_Flip_Flop #(.trigger("falling")) j_k_ff_6 (
    .J(1'b1), .clk(j_k_ff_2_q[1]), .K(1'b1), .Q(j_k_ff_2_q[2]), .reset(and_2_out));  // open: Qn, preset, en
  J_K_Flip_Flop #(.trigger("falling")) j_k_ff_7 (
    .J(1'b1), .clk(j_k_ff_1_q[2]), .K(1'b1), .Q(j_k_ff_1_q[3]), .reset(and_1_out));  // open: Qn, preset, en
  J_K_Flip_Flop #(.trigger("falling")) j_k_ff_8 (
    .clk(j_k_ff_1_q[3]), .Q(j_k_ff_1_q[4]));  // open: J, K, Qn, preset, en, reset
  J_K_Flip_Flop #(.trigger("falling")) j_k_ff_9 (
    .clk(j_k_ff_2_q[3]), .Q(j_k_ff_2_q[4]));  // open: J, K, Qn, preset, en, reset
  J_K_Flip_Flop #(.trigger("falling")) j_k_ff_10 (
    .J(1'b1), .clk(j_k_ff_2_q[2]), .K(1'b1), .Q(j_k_ff_2_q[3]), .reset(and_2_out));  // open: Qn, preset, en
  J_K_Flip_Flop #(.trigger("falling")) j_k_ff_11 (
    .clk(j_k_ff_1_q[4]), .Q(j_k_ff_1_q[5]));  // open: J, K, Qn, preset, en, reset
  J_K_Flip_Flop #(.trigger("falling")) j_k_ff_12 (
    .clk(j_k_ff_2_q[4]), .Q(j_k_ff_2_q[5]));  // open: J, K, Qn, preset, en, reset
endmodule
