// Logisim project Somador 8 bits.circ as structural Verilog: 1 circuit, main circuit main
module main (
  input  [7:0] A,
  input  [7:0] B,
  input  in_3,
  output [7:0] S
);

  wire main_1_cout, main_3_cout, main_4_cout, main_5_cout, main_6_cout, main_7_cout, main_8_cout;

  Contador_main main_1 (.Cout(main_1_cout), .S(S[6]), .A(A[6]), .B(B[6]), .Cin(main_3_cout));
  Contador_main main_2 (.S(S[7]), .A(A[7]), .B(B[7]), .Cin(main_1_cout));  // open: Cout
  Contador_main main_3 (.Cout(main_3_cout), .S(S[5]), .A(A[5]), .B(B[5]), .Cin(main_5_cout));
  Contador_main main_4 (.Cout(main_4_cout), .S(S[3]), .A(A[3]), .B(B[3]), .Cin(main_7_cout));
  Contador_main main_5 (.Cout(main_5_cout), .S(S[4]), .A(A[4]), .B(B[4]), .Cin(main_4_cout));
  Contador_main main_6 (.Cout(main_6_cout), .S(S[1]), .A(A[1]), .B(B[1]), .Cin(main_8_cout));
  Contador_main main_7 (.Cout(main_7_cout), .S(S[2]), .A(A[2]), .B(B[2]), .Cin(main_6_cout));
  Contador_main main_8 (.Cout(main_8_cout), .S(S[0]), .A(A[0]), .B(B[0]), .Cin(in_3));
endmodule
