// Logisim project somador de 8 bits.circ as structural Verilog: 1 circuit, main circuit main
module main (
  input  in_1,
  input  in_2,
  input  in_3,
  input  in_4,
  input  in_5,
  input  in_6,
  input  in_7,
  input  in_8,
  input  in_9,
  input  in_10,
  input  in_11,
  input  in_12,
  input  in_13,
  input  in_14,
  input  in_15,
  input  in_16,
  input  in_17,
  output out_18,
  output out_19,
  output out_20,
  output out_21,
  output out_22,
  output out_23,
  output out_24,
  output out_25,
  output out_26
);

  wire main_1_p4, main_2_p5, main_3_p5, main_4_p4, main_4_p6, main_6_p5, main_7_p5;

  // Contador_main main_1: pin names not known; wires that end beside it: in_9, out_26, in_1, main_1_p4, out_18
  // Contador_main main_2: pin names not known; wires that end beside it: out_18, in_10, main_1_p4, in_2, main_2_p5, out_19
  // Contador_main main_3: pin names not known; wires that end beside it: out_19, in_11, main_2_p5, in_3, main_3_p5, out_20
  // Contador_main main_4: pin names not known; wires that end beside it: out_21, out_21, in_13, main_4_p4, in_5, main_4_p6, out_22
  // Contador_main main_5: pin names not known; wires that end beside it: out_20, in_12, main_3_p5, in_4, main_4_p4, out_21, out_21
  // Contador_main main_6: pin names not known; wires that end beside it: out_22, in_14, main_4_p6, in_6, main_6_p5, out_23
  // Contador_main main_7: pin names not known; wires that end beside it: out_23, in_15, main_6_p5, in_7, main_7_p5, out_24
  // Contador_main main_8: pin names not known; wires that end beside it: out_24, in_16, main_7_p5, in_8, in_17, out_25
endmodule
