// Logisim project subtrator de 8 bits.circ as structural Verilog: 1 circuit, main circuit main
module main (
  input  B,
  input  B_2,
  input  B_3,
  input  B_4,
  input  B_5,
  input  B_6,
  input  B_7,
  input  B_8,
  input  A,
  input  A_2,
  input  A_3,
  input  A_4,
  input  A_5,
  input  A_6,
  input  A_7,
  input  A_8,
  input  in_17,
  output out_18,
  output out_19,
  output out_20,
  output out_21,
  output out_22,
  output out_23,
  output out_24,
  output out_25,
  output out_26
);

  wire main_2_cout, main_3_cout, main_4_cout, main_5_cout, main_6_cout, main_7_cout, main_8_cout;

  subtrator_main main_1 (.S(out_18), .Cout(out_26), .A(A), .B(B), .Cin(main_2_cout));
  subtrator_main main_2 (.S(out_19), .Cout(main_2_cout), .A(A_2), .B(B_2), .Cin(main_3_cout));
  subtrator_main main_3 (.S(out_20), .Cout(main_3_cout), .A(A_3), .B(B_3), .Cin(main_5_cout));
  subtrator_main main_4 (.S(out_22), .Cout(main_4_cout), .A(A_5), .B(B_5), .Cin(main_6_cout));
  subtrator_main main_5 (.S(out_21), .Cout(main_5_cout), .A(A_4), .B(B_4), .Cin(main_4_cout));
  subtrator_main main_6 (.S(out_23), .Cout(main_6_cout), .A(A_6), .B(B_6), .Cin(main_7_cout));
  subtrator_main main_7 (.S(out_24), .Cout(main_7_cout), .A(A_7), .B(B_7), .Cin(main_8_cout));
  subtrator_main main_8 (.S(out_25), .Cout(main_8_cout), .A(A_8), .B(B_8), .Cin(in_17));
endmodule
