// Logisim project Contador.circ as structural Verilog: 1 circuit, main circuit main
module main (
  input  A,
  input  B,
  input  Cin,
  output Cout,
  output S
);

  wire and_1_out, and_2_out, and_3_out, xor_1_out;

  and and_1 (and_1_out, A, B);
  and and_2 (and_2_out, A, Cin);
  and and_3 (and_3_out, B, Cin);
  xor xor_1 (xor_1_out, Cin, B);
  or or_1 (Cout, and_1_out, and_2_out, and_3_out);
  xor xor_2 (S, xor_1_out, A);
endmodule
