// Logisim project Somador 8 bits mais e menos.circ as structural Verilog: 1 circuit, main circuit main
module main (
  input  [7:0] A,
  input  [7:0] B,
  input  Op,
  output [7:0] S
);

  wire main_1_cout, main_2_cout, main_3_cout, main_4_cout, main_5_cout, main_6_cout, main_7_cout,
       main_8_cout, xor_1_out, xor_2_out, xor_3_out, xor_4_out, xor_5_out, xor_6_out, xor_7_out, xor_8_out;

  xor xor_1 (xor_1_out, B[7], Op);
  xor xor_2 (xor_2_out, B[6], Op);
  Contador_main main_1 (.Cout(main_1_cout), .S(S[6]), .A(A[6]), .B(xor_2_out), .Cin(main_3_cout));
  Contador_main main_2 (.Cout(main_2_cout), .S(S[7]), .A(A[7]), .B(xor_1_out), .Cin(main_1_cout));
  xor xor_3 (xor_3_out, B[5], Op);
  Contador_main main_3 (.Cout(main_3_cout), .S(S[5]), .A(A[5]), .B(xor_3_out), .Cin(main_4_cout));
  xor xor_4 (xor_4_out, B[3], Op);
  xor xor_5 (xor_5_out, B[4], Op);
  Contador_main main_4 (.Cout(main_4_cout), .S(S[4]), .A(A[4]), .B(xor_5_out), .Cin(main_5_cout));
  Contador_main main_5 (.Cout(main_5_cout), .S(S[3]), .A(A[3]), .B(xor_4_out), .Cin(main_6_cout));
  xor xor_6 (xor_6_out, B[1], Op);
  xor xor_7 (xor_7_out, B[2], Op);
  Contador_main main_6 (.Cout(main_6_cout), .S(S[2]), .A(A[2]), .B(xor_7_out), .Cin(main_7_cout));
  Contador_main main_7 (.Cout(main_7_cout), .S(S[1]), .A(A[1]), .B(xor_6_out), .Cin(main_8_cout));
  xor xor_8 (xor_8_out, B[0], Op);
  Contador_main main_8 (.Cout(main_8_cout), .S(S[0]), .A(A[0]), .B(xor_8_out), .Cin(Op));
endmodule
