// Logisim project ULA.circ as structural Verilog: 4 circuits, main circuit main
module main (
  input  [3:0] A,
  input  [3:0] B,
  input  [1:0] Op,
  input  in_4
);

  wire [3:0] and_5_out, and_6_out, and_7_out, and_8_out, and_9_out, main_1_s, multiplier_1_out, or_1_out,
       or_2_out;
  wire [3:3] and_1_out, and_2_out, and_3_out, and_4_out;

  and and_1 (and_1_out[3], ~Op[0], ~Op[1]);  // AND_Gate
  and and_2 (and_2_out[3], Op[0], ~Op[1]);  // AND_Gate
  and and_3 (and_3_out[3], ~Op[0], Op[1]);  // AND_Gate
  and and_4 (and_4_out[3], Op[0], Op[1]);
  // Probe on and_5_out
  assign and_5_out = A & B;  // AND_Gate and_5, 4 bits wide
  // Probe on or_1_out
  assign or_1_out = A | B;  // OR_Gate or_1, 4 bits wide
  // Probe on main_1_s
  Somador4bits_main main_1 (.A(A), .B(B), .in_3(in_4), .S(main_1_s));
  // Probe on multiplier_1_out
  Multiplier #(.width(4)) multiplier_1 (.a(A), .b(B), .out(multiplier_1_out));  // open: cin, cout
  // Probe on and_6_out
  assign and_6_out = and_5_out & {4{and_1_out[3]}};  // AND_Gate and_6, 4 bits wide
  // Probe on and_7_out
  assign and_7_out = or_1_out & {4{and_2_out[3]}};  // AND_Gate and_7, 4 bits wide
  // Probe on and_8_out
  assign and_8_out = main_1_s & {4{and_3_out[3]}};  // AND_Gate and_8, 4 bits wide
  // Probe on and_9_out
  assign and_9_out = multiplier_1_out & {4{and_4_out[3]}};  // AND_Gate and_9, 4 bits wide
  assign or_2_out = and_6_out | and_7_out | and_8_out | and_9_out;  // OR_Gate or_2, 4 bits wide
  // Probe on or_2_out
endmodule

module Escolha (
  input  [3:0] in_1,
  input  [3:0] in_2,
  input  [1:0] in_3
);

  main main_1 (.A(in_1), .B(in_2), .Op(in_3));  // open: in_4
endmodule

module Contador (
  input  A,
  input  B,
  input  Cin,
  output S,
  output Cout
);

  wire and_1_out, and_2_out, and_3_out, xor_1_out;

  and and_1 (and_1_out, Cin, B);
  and and_2 (and_2_out, Cin, A);
  and and_3 (and_3_out, B, A);
  xor xor_1 (xor_1_out, A, B);
  or or_1 (S, and_1_out, and_2_out, and_3_out);
  xor xor_2 (Cout, xor_1_out, Cin);
endmodule

module Somador8bits (
  input  [7:0] A,
  input  [7:0] B
);
endmodule
