// Logisim project Somador4bits.circ as structural Verilog: 1 circuit, main circuit main
module main (
  input  [3:0] A,
  input  [3:0] B,
  input  in_3,
  output [3:0] S
);

  wire main_2_cout, main_3_cout, main_4_cout;

  Contador_main main_1 (.S(S[3]), .A(A[3]), .B(B[3]), .Cin(main_2_cout));  // open: Cout
  Contador_main main_2 (.Cout(main_2_cout), .S(S[2]), .A(A[2]), .B(B[2]), .Cin(main_3_cout));
  Contador_main main_3 (.Cout(main_3_cout), .S(S[1]), .A(A[1]), .B(B[1]), .Cin(main_4_cout));
  Contador_main main_4 (.Cout(main_4_cout), .S(S[0]), .A(A[0]), .B(B[0]), .Cin(in_3));
endmodule
